# Fritzing sketch Diagrama (saved by Fritzing 0.9.3b)
breadboards: 1

parts:
  Componente1 = Arduino Board Ethernet
  J1 = Basic Servo
  RHT1 = Humidity and Temperature Sensor RHT03
  LED1 = smd LED [color="Red (633nm)" package="0805 [SMD]"]  # not connected
  R1 = Resistor [tolerance=±5% resistance=220 package=THT]
  R2 = PHOTOCELL [package=photocell-kit]
  R3 = Resistor [tolerance=±5% resistance=220 package=THT]

nets:
  N1: Componente1.A0, R2.P$2, R3.Pin_1
  N2: Componente1.D2_PWM, RHT1.Data-signal
  N3: Componente1.D7, J1.pulse
  N4: RHT1.Vcc, R3.Pin_0
  N5: RHT1.GND_2, R1.Pin_0, R2.P$1
